# Fritzing sketch three_blinking_leds (saved by Fritzing 0.9.3b)
breadboards: 1

parts:
  Part1 = Arduino Uno (Rev3)
  R1 = Resistor [tolerance=±5% resistance=220 package=THT]
  LED1 = LED - 5mm [color="Red (633nm)" package="5 mm [THT]"]
  R2 = Resistor [tolerance=±5% resistance=220 package=THT]
  R3 = Resistor [tolerance=±5% resistance=220 package=THT]
  LED2 = LED - 5mm [color="Red (633nm)" package="5 mm [THT]"]
  LED3 = LED - 5mm [color="Red (633nm)" package="5 mm [THT]"]

nets:
  N1: Part1.GND, LED1.cathode, LED2.cathode, LED3.cathode
  N2: Part1.D1/TX, R1.Pin_0
  N3: Part1.D2, R2.Pin_0
  N4: Part1.D3_PWM, R3.Pin_0
  N5: R2.Pin_1, LED2.anode
  N6: R3.Pin_1, LED3.anode
